# Fritzing sketch Strom2HoTT (saved by Fritzing 0.9.2b)

parts:
  Bauteil1 = Arduino Pro Mini v13
  part = female pin header, 3 pins [form="♀ (female)" part_number=Empfänger]
  R1 = Resistor [tolerance=±0.05% resistance=1.8k package=THT]
  D1 = Zener Diode [part_number="Z-Diode 3,3V" breakdown_voltage=3.3V package="Melf DO-213 AB [SMD]"]
  part_2 = female pin header, 1 pin [form="♀ (female)" part_number="Spannung 0-5V"]
  part_3 = rounded female pin header, 1 pin [form="♀ (female rounded)" part_number="Strom 0-5V"]

nets:
  N1: Bauteil1.RAW, part.pin2
  N2: Bauteil1.GND, part.pin1, D1.anode
  N3: Bauteil1.A1, part_3.pin1
  N4: Bauteil1.A0, part_2.pin1
  N5: Bauteil1.D3_PWM, R1.Pin_1
  N6: part.pin3, R1.Pin_0, D1.cathode

notes:
  -
  +
  T
